# Fritzing sketch DigitalLinearSupply (saved by Fritzing 0.9.0b)

parts:
  C1 = Ceramic Capacitor [capacitance=100nF package="100 mil [THT, multilayer]"]
  C2 = Ceramic Capacitor [capacitance=100nF package="100 mil [THT, multilayer]"]
  Power_plug1 = Power plug
  Power_plug2 = Power plug
  U1 = LM 358 Dual Op-Amp [package="SO 08 [SMD]"]
  Part1 = Arduino Pro Mini v13
  R3 = Resistor [tolerance=±5% resistance=470 package=THT]
  R4 = Resistor [tolerance=±10% resistance=6.8k package=THT]
  R5 = Resistor [tolerance=±10% resistance=10k package=THT]
  C3 = Ceramic Capacitor [capacitance=100nF package="100 mil [THT, multilayer]"]
  C4 = Electrolytic Capacitor [capacitance=1µF package="100 mil [THT, electrolytic]"]
  U2 = Voltage Regulator - Variable [package="TO220 [THT]"]
  M1 = DC Motor
  R6 = Resistor [tolerance=±20% resistance=10k package=THT]
  R7 = Resistor [tolerance=±20% resistance=10k package=THT]
  F1 = Resettable Fuse PTC [package=ptc]

nets (from the breadboard view):
  N1: C1.0, R6.Pin_1, R7.Pin_0
  GND: C1.1, C2.1, Power_plug1.GND, Power_plug2.GND, U1.connector3, Part1.GND, R5.Pin_0, C3.1, C4.+, M1.pin_2
  N2: C2.0, U1.connector2, R7.Pin_1
  N3: Power_plug1.VCC, U1.connector7, C3.0, U2.IN
  VCC: Power_plug2.VCC, Part1.VCC
  N4: U1.connector0, R3.Pin_0, R4.Pin_1, U2.ADJ
  N5: U1.connector1, R4.Pin_0, R5.Pin_1
  N6: Part1.D10_PWM/SS, R6.Pin_0
  N7: R3.Pin_1, C4.-, U2.OUT, F1.1
  N8: M1.pin_1, F1.2

notes:
  Low pass filter to turn PWM into analog voltage
  5V Power Supply
  12V Power Supply
  Square Wave/PWM
  from Arduino
  Op Amp to convert 5V to ~8.75V (more like 8.4V)
  Gain = 1 + (F/G)
  (1 + 6.8/10) = 1.68
  F
  G
  LM317 Receives 0-8.75V and then outputs that + 1.25V to motor to give about 1.25-10V control of motor.
  We'll actually send power into h-bridge to be able to control
  direction of motor.
  10KΩ
  100nF
  6.8KΩ
  470Ω
  1µF
  500mA Resetable PTC Fuse
