# Fritzing sketch circuit (saved by Fritzing 0.9.0b)

parts:
  Part1 = Logic Level Converter
  Part2 = Arduino Pro Mini v13
  IC1 = H-Bridge [package=THT]
  ULN1 = Darlington Driver [package=dil18]  # not connected
  Raspberry_Pi1 = Raspberry Pi B rev2
  U1 = QRD1114 [package=qrd1114]  # not connected
  U2 = QRD1114 [package=qrd1114]  # not connected
  U3 = QRD1114 [package=qrd1114]  # not connected
  U4 = QRD1114 [package=qrd1114]
  U5 = QRD1114 [package=qrd1114]  # not connected
  U6 = QRD1114 [package=qrd1114]  # not connected
  L1 = Solenoid  # not connected
  L2 = Solenoid  # not connected
  L3 = Solenoid  # not connected
  M1 = DC Motor
  Power_plug1 = Power plug
  Q1 = NPN-Transistor [package="TO92 [THT]"]
  R1 = Resistor [tolerance=±5% resistance=220 package=THT]
  R2 = Resistor [tolerance=±20% resistance=5.6k package=THT]
  Power_plug2 = Power plug

nets:
  N1: Part1.TX2_LV, Raspberry_Pi1.GPIO_15
  N2: Part1.RX2_LV, Raspberry_Pi1.GPIO_14
  GND: Part1.GND, Part2.GND, IC1.GND4, Raspberry_Pi1.GND, U4.C, U4.K, Power_plug1.GND, Power_plug2.GND
  N3: Part1.LV, Raspberry_Pi1.3V3
  VCC: Part1.HV, Part2.VCC, IC1.VCC1, Power_plug1.VCC, Q1.C, R2.Pin_0
  N4: Part1.RX2_HV, Part2.D0/TX
  N5: Part1.TX2_HV, Part2.D1/RX
  N6: Part2.A0, U4.E, R2.Pin_1
  N7: Part2.D9_PWM, IC1.1_2EN
  N8: Part2.D8, IC1.2A
  N9: Part2.D7, IC1.1A
  N10: Part2.D2, Q1.B
  N11: IC1.1Y, M1.pin_2
  N12: IC1.2Y, M1.pin_1
  N13: IC1.VCC2, Power_plug2.VCC
  N14: U4.A, R1.Pin_1
  N15: Q1.E, R1.Pin_0

notes:
  5 Volt Power
  10 Volt Power
  train throttle
